# Fritzing sketch clock-module (saved by Fritzing 1.0.6)
circuit board: 8.46667cm x 5.64444cm
breadboards: 1

parts:
  U1 = 555 Timer [package="DIP8 [THT]"]
  C1 = Ceramic Capacitor [capacitance=1µF voltage=6.3V package="100 mil [THT, multilayer]"]
  LED1_(built-in_R) = LED - 3mm [color="Red (633nm)" current=0.030A package="3 mm [THT]"]
  C2 = Ceramic Capacitor [capacitance=0.01µF voltage=35V package="100 mil [THT, multilayer]"]
  R2 = Resistor [tolerance=±5% power=0.25W resistance=1k package=THT]
  VCC1 = 4 x AAA Battery Mount [internal_resistance=0.1Ω]
  R1 = Resistor [tolerance=±5% resistance=1k power=0.25W package=THT]
  RV1 = POT [mpn=91AR1MEGLF part_number=91AR1MEGLF]

nets:
  N1: U1.Ground, C1.1, LED1_(built-in_R).cathode, C2.1, VCC1.-
  N2: U1.Trigger, U1.Threshold, C1.0, RV1.S, RV1.A
  N3: U1.Output, LED1_(built-in_R).anode
  N4: U1.Reset, U1.Vcc_Supply_Voltage, VCC1.+, R1.Pin_0
  N5: U1.Control_Voltage, C2.0
  N6: U1.Discharge, R2.Pin_0, R1.Pin_1
  N7: R2.Pin_1, RV1.E
